// Logisim project circuitos.circ as structural Verilog: 2 circuits, main circuit main
module main (
  input  A,
  input  B,
  input  C,
  output S2
);

  exemplo2 exemplo2_1 (.A(A), .B(B), .C(C), .out_4(S2));
endmodule

module exemplo2 (
  input  A,
  input  B,
  input  C,
  output out_4
);

  wire and_1_out, not_1_out, not_2_out, not_3_out, or_1_out, xor_1_out;

  xor xor_1 (xor_1_out, A, B);
  not not_1 (not_1_out, B);
  or or_1 (or_1_out, xor_1_out, not_1_out);
  not not_2 (not_2_out, A);
  not not_3 (not_3_out, C);
  and and_1 (and_1_out, or_1_out, not_2_out);
  or or_2 (out_4, and_1_out, not_3_out);
endmodule
